# Fritzing sketch all_components_assemble_scheme (saved by Fritzing 0.9.3b)
perfboards: 1

parts:
  MCU1 = Raspberry Pi Zero  # not connected
  J1 = shrouded pin header, 40 pins [form="♂ (shrouded male)"]
  DS1 = DS18B20 1-Wire Temperature Sensor [part_number=DS18B20]
  DS2 = DS18B20 1-Wire Temperature Sensor [part_number=DS18B20]
  DS3 = DS18B20 1-Wire Temperature Sensor [part_number=DS18B20]
  DS4 = DS18B20 1-Wire Temperature Sensor [part_number=DS18B20]
  R1 = Resistor [tolerance=±5% resistance=4.7k package=THT]
  JP1 = Header 10 [package=1x10-2mm-smd]
  Relay1 = DIP - 20 pins [chip_label=Relay package="DIP (Dual Inline) [THT]"]  # not connected

nets:
  N1: J1.pin4, DS1.DQ, DS2.DQ, DS3.DQ, DS4.DQ, R1.Pin_1
  N2: J1.pin5, JP1.1
  N3: J1.pin6, JP1.2
  N4: J1.pin7, JP1.3
  N5: J1.pin8, JP1.4
  GND: J1.pin9, DS1.GND, DS2.GND, DS3.GND, DS4.GND, R1.Pin_0
  N6: J1.pin19, JP1.9
  N7: J1.pin23, JP1.8
  N8: J1.pin30, JP1.7
  VDD: J1.pin31, DS1.VDD, DS2.VDD, DS3.VDD, DS4.VDD
  N9: J1.pin32, JP1.6
  N10: J1.pin33, JP1.5
  N11: J1.pin40, JP1.10

custom parts:
  DIP - 20 pins: Relay 8-channels
