# Fritzing sketch brewery (saved by Fritzing 0.9.3b)
breadboards: 1

parts:
  MCU1 = Raspberry Pi Zero
  R1 = Resistor [tolerance=±5% resistance=4.7k package=THT]
  DS1 = DS18B20 1-Wire Temperature Sensor [part_number=DS18B20]
  DS2 = DS18B20 1-Wire Temperature Sensor [part_number=DS18B20]
  DS3 = DS18B20 1-Wire Temperature Sensor [part_number=DS18B20]

nets:
  VDD: MCU1.pin_1, MCU1.pin_17, R1.Pin_1, DS1.VDD, DS2.VDD, DS3.VDD
  GND: MCU1.pin_6, MCU1.pin_20, MCU1.pin_25, DS1.GND, DS2.GND, DS3.GND
  N1: MCU1.pin_7, R1.Pin_0, DS1.DQ, DS2.DQ, DS3.DQ
